# Fritzing sketch montage (saved by Fritzing 0.9.3b)

parts:
  Part1 = Adafruit Pro Trinket 5V 16MHz [part_number="Adafruit #2000"]
  Part2 = Adafruit Feather HUZZAH ESP8266 [part_number="Adafruit #2821"]
  JACK1 = 2.1mm Barrel Jack with Terminal Block
  Q2 = TIP120 Hi-Current Darlington Transistor
  Q3 = TIP120 Hi-Current Darlington Transistor
  NEOPIXEL2 = Neopixel Strip -- White (30/m)
  M1 = DC Motor
  D1 = Diode [package=diode-hv]
  NEOPIXEL1 = Neopixel Strip -- White (30/m)
  U1 = Voltage Regulator - 5V [package="TO220 [THT]"]

nets:
  N1: Part1.RXD, Part2.GPIO12/MISO
  N2: Part1.VBAT, JACK1.POS
  N3: Part1.TXD, Part2.GPIO14/SCK
  N4: Part1.D11, Q2.BASE
  N5: Part1.A0, Q3.BASE
  N6: Part2.VBAT, U1.output_voltage
  N7: JACK1.NEG, U1.GND
  GND: Q2.COLLECTOR, NEOPIXEL2.GND, NEOPIXEL1.GND
  N8: Q3.COLLECTOR, M1.pin_1
  N9: M1.pin_2, D1.C

notes:
  Pump
  Alim 12v 3A
  (ours don't have data pin)
  Water Lvl Sensors
  (Capacitive Without Hardware)
  Feather Huzzah
  Trinket Pro 5v
  LED Strips

custom parts:
  Adafruit Pro Trinket 5V 16MHz: Trinket's got a big sister in town - the Pro Trinket 5V! Pro Trinket combines everything you love about Trinket with the familiarity of the common core Arduino chip, the ATmega328. It's like an Arduino Pro Mini with more pins and USB tossed in, so delicious. Trinket's a year old now, and while its been great to see tons of tiny projects, sometimes you just need more pins, more FLASH, and more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
  Adafruit Feather HUZZAH ESP8266: his is the Adafruit Feather HUZZAH ESP8266 - our take on an 'all-in-one' ESP8266 WiFi development board with built in USB and battery charging. Its an ESP8266 WiFi module with all the extras you need, ready to rock! We have other boards in the Feather family, check'em out here. At the Feather HUZZAH's heart is an ESP8266 WiFi microcontroller clocked at 80 MHz and at 3.3V logic. This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
  Neopixel Strip -- White (30/m): These NeoPixel strips have 30 digitally-addressable pixel LEDs per meter and are very affordable and are only 12.5 mm wide, 10 mm if you remove the strip from the casing.
